# Fritzing sketch Graphical System (saved by Fritzing 0.9.10b)
breadboards: 1

parts:
  SG1 = Buzzer 12mm [package=buzzer-12mm-ns]
  Part1 = Arduino Uno (Rev3) - ICSP
  HC-SR04_Sensor_1 = HC-SR04 Ultrasonic Distance Sensor
  LED1 = smd LED [color="Green (565nm)" package="0603 [SMD]"]
  LED2 = LED - 5mm [color="Yellow (585nm)" current=0.030 package="5 mm [THT]"]
  LED3 = smd LED [color="Red (633nm)" package="1206 [SMD]"]

nets:
  N1: SG1.1, Part1.D8
  N2: SG1.2, HC-SR04_Sensor_1.GND, LED1.anode, LED2.anode, LED3.anode
  N3: Part1.D9_PWM, HC-SR04_Sensor_1.TRIG
  N4: Part1.D10_PWM/SS, HC-SR04_Sensor_1.ECHO
  N5: Part1.D4, LED1.cathode
  N6: Part1.D5_PWM, LED2.cathode
  N7: Part1.D6_PWM, LED3.cathode
